# Fritzing sketch open-race-scale-pi-hat-v1 (saved by Fritzing 0.9.3b)
circuit board: 8.53488cm x 5.63626cm

parts:
  LC1 = HX711 Weighing Sensor Module
  LC2 = HX711 Weighing Sensor Module
  LC3 = HX711 Weighing Sensor Module
  LC4 = HX711 Weighing Sensor Module
  FL = screw terminal, 4 pins
  FR = screw terminal, 4 pins
  RL = screw terminal, 4 pins
  RR = screw terminal, 4 pins
  P2 = Pad [width=2 height=2 connect=center]
  P1 = Pad [width=2 height=2 connect=center]
  J1 = female pin header, 4 pins [form="♀ (female)"]
  P3 = Pad [width=2 height=2 connect=center]
  P4 = Pad [width=2 height=2 connect=center]
  P1_2 = Pad [width=2 height=2 connect=center]
  Raspberry_Pi_1 = Raspberry Pi 3 [part_number=RPI-3-V1.2]

nets:
  VCC: LC1.VCC, LC2.VCC, LC3.VCC, LC4.VCC, P1.pad, J1.pin3, P3.pad, P1_2.pad, Raspberry_Pi_1.5V
  GND: LC1.GND, LC2.GND, LC3.GND, LC4.GND, J1.pin1, Raspberry_Pi_1.GND
  N1: LC1.DO/RX, Raspberry_Pi_1.GPIO17
  N2: LC1.CK/TX, Raspberry_Pi_1.GPIO27
  N3: LC1.E+, FL.pin4
  N4: LC1.E-, FL.pin3
  N5: LC1.A+, FL.pin2
  N6: LC1.A-, FL.pin1
  N7: LC2.DO/RX, Raspberry_Pi_1.GPIO22
  N8: LC2.CK/TX, Raspberry_Pi_1.GPIO23
  N9: LC2.E+, FR.pin4
  N10: LC2.E-, FR.pin3
  N11: LC2.A+, FR.pin2
  N12: LC2.A-, FR.pin1
  N13: LC3.DO/RX, Raspberry_Pi_1.GPIO5
  N14: LC3.CK/TX, Raspberry_Pi_1.GPIO6
  N15: LC3.E+, RL.pin4
  N16: LC3.E-, RL.pin3
  N17: LC3.A+, RL.pin2
  N18: LC3.A-, RL.pin1
  N19: LC4.DO/RX, Raspberry_Pi_1.GPIO16
  N20: LC4.CK/TX, Raspberry_Pi_1.GPIO26
  N21: LC4.E+, RR.pin4
  N22: LC4.E-, RR.pin3
  N23: LC4.A+, RR.pin2
  N24: LC4.A-, RR.pin1
  N25: P2.pad, J1.pin2, Raspberry_Pi_1.3v3
  5V: J1.pin4, P4.pad

notes:
  Red -> E+
  Black -> E-
  Green -> A+
  White -> A-
  To FL Load Cell
  To FR Load Cell
  To RL Load Cell
  To RR Load Cell
  E+
  Power Header
  (optional)
  Open Race Scale V1.0
